# Fritzing sketch SIM800L_ESP32_RFID (saved by Fritzing 0.9.4)

parts:
  MH-ET_LIVE_ESP32_DEVKIT1 = MH-ET LIVE ESP32 DEVKIT 38 pins
  GSM_SIM_GPSR_SMS_SIM900_SIM1 = SIM800L [package=THT]
  Part1 = RFID-RC522-v2

nets:
  3V3: MH-ET_LIVE_ESP32_DEVKIT1.3V3, Part1.3.3V
  GND: MH-ET_LIVE_ESP32_DEVKIT1.GND, GSM_SIM_GPSR_SMS_SIM900_SIM1.GND
  5V: MH-ET_LIVE_ESP32_DEVKIT1.5V, GSM_SIM_GPSR_SMS_SIM900_SIM1.5V
  N1: MH-ET_LIVE_ESP32_DEVKIT1.IO23, Part1.MOSI
  N2: MH-ET_LIVE_ESP32_DEVKIT1.IO22, Part1.RST
  N3: MH-ET_LIVE_ESP32_DEVKIT1.IO21, Part1.SDA
  N4: MH-ET_LIVE_ESP32_DEVKIT1.IO19, Part1.MISO
  N5: MH-ET_LIVE_ESP32_DEVKIT1.IO18, Part1.SCK
  N6: MH-ET_LIVE_ESP32_DEVKIT1.IO4, GSM_SIM_GPSR_SMS_SIM900_SIM1.SIM_RXD
  N7: MH-ET_LIVE_ESP32_DEVKIT1.IO15, GSM_SIM_GPSR_SMS_SIM900_SIM1.SIM_TXD

custom parts:
  MH-ET LIVE ESP32 DEVKIT 38 pins: http://mh.nodebb.com/topic/2/mh-et-live-esp32-devkit
  RFID-RC522-v2: A simple China made RFID-RC522 Reader; do check the pin labels, as this is a MFRC522 based clone.
